// Logisim project 111.circ as structural Verilog: 1 circuit, main circuit main
module main (
  input  azud0,
  input  azud1,
  input  azud2,
  input  azud3,
  input  azud4,
  input  azud5,
  input  azud6,
  input  azud7
);

  wire and_1_out, and_2_out, and_3_out, and_4_out, and_5_out, and_6_out, and_7_out, and_8_out, nor_1_out,
       nor_2_out, nor_3_out, or_1_out, or_2_out, xor_1_out, xor_2_out, xor_3_out, xor_4_out, xor_5_out,
       xor_6_out, xor_7_out;

  and and_1 (and_1_out, azud0, azud1);
  and and_2 (and_2_out, azud2, azud3);
  and and_3 (and_3_out, azud4, azud5);
  and and_4 (and_4_out, azud6, azud7);
  nor nor_1 (nor_1_out, azud0, azud1, azud2, azud3, azud4, azud5, azud6, azud7);
  xor xor_1 (xor_1_out, azud0, azud1);
  xor xor_2 (xor_2_out, azud2, azud3);
  xor xor_3 (xor_3_out, azud4, azud5);
  xor xor_4 (xor_4_out, azud6, azud7);
  and and_5 (and_5_out, xor_1_out, xor_2_out);
  xor xor_5 (xor_5_out, xor_3_out, xor_4_out);
  and and_6 (and_6_out, xor_3_out, xor_4_out);
  xor xor_6 (xor_6_out, xor_1_out, xor_2_out);
  or or_1 (or_1_out, and_5_out, and_1_out, and_2_out);
  or or_2 (or_2_out, and_6_out, and_3_out, and_4_out);
  and and_7 (and_7_out, xor_7_out, nor_3_out);
  xor xor_7 (xor_7_out, xor_6_out, xor_5_out);
  and and_8 (and_8_out, xor_6_out, xor_5_out);
  nor nor_2 (nor_2_out, and_7_out, nor_1_out);
  nor nor_3 (nor_3_out, and_8_out, or_1_out, or_2_out);
endmodule
